# Fritzing sketch Autohelm 800 ESP32 Retrofit v2 (saved by Fritzing 0.9.6b)
circuit board: 8.46667cm x 5.64444cm

parts:
  JP1 = Header 5x2 [package=avr_icsp]
  LOLIN32_LITE = Wemos Lolin32lite
  J1 = Power Jack [package=power_jack_smd]
  M1 = DC Motor
  U2 = Mini-360 DC-DC Buck converter [package=THT]
  Mod2 = MAX-471 [package=THT]
  Part1 = Adafruit DRV8871 [part_number="Adafruit #3190"]

nets:
  N1: JP1.3, LOLIN32_LITE.pin_16
  N2: JP1.5, LOLIN32_LITE.pin_10
  N3: JP1.6, LOLIN32_LITE.pin_9
  N4: JP1.7, LOLIN32_LITE.pin_11
  N5: JP1.8, LOLIN32_LITE.pin_13, Mod2.gnd#0, Mod2.gnd#6, Mod2.gnd#7, Part1.GND
  N6: JP1.9, LOLIN32_LITE.pin_12
  N7: JP1.10, LOLIN32_LITE.pin_8
  N8: LOLIN32_LITE.pin_4, Mod2.VT
  N9: LOLIN32_LITE.pin_5, LOLIN32_LITE.pin_28, J1.GND, U2.IN-, Mod2.vout, Mod2.gnd#2, Mod2.AT, Part1.VMOTOR
  N10: LOLIN32_LITE.pin_14, U2.OUT+
  N11: LOLIN32_LITE.pin_15, U2.OUT-
  N12: LOLIN32_LITE.pin_20, Part1.IN1
  N13: LOLIN32_LITE.pin_21, Part1.IN2
  N14: J1.GNDBREAK, U2.IN+, Mod2.vin
  N15: M1.pin_1, Part1.OUT2
  N16: M1.pin_2, Part1.OUT1

notes:
  Keypad V2

custom parts:
  Wemos Lolin32lite: Wemos Lolinlite32 wifi and blue tooth board based on the ESP-32 cpu, digital I/Os 19, analog inputs 6, clock 240mhz, Flash 4Mbytes, lipo battery charger (500ma connection broken out on breadboard but not pcb), usb.
  Mini-360 DC-DC Buck converter: Mini-360 DC-DC Buck converter. Tiny buck step down voltage converter, input voltage 4.75 to 23V output 1 to 17V adjustable. Available from ebay and the like.
  MAX-471: MAX471 Current detection module. 3-36V, 0-3A
  Adafruit DRV8871: Crank up your robotics with powerful Adafruit DRV8871 motor driver breakout board. This motor driver has a lot of great specs that make it useful for a wide variety of mechatronics. In particular, the simple resistor-set current limiting and auto-magic PWM support make it super easy to use. Check out the specs for the DRV8871: 6.5V to 45V motor power voltage Up to 5.5V logic level on IN pins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
