# Fritzing sketch Autohelm 800 ESP32 Retrofit v3 (saved by Fritzing 0.9.6b)
circuit board: 5.48968cm x 6.70738cm

parts:
  JP1 = Header 5x2 [package=avr_icsp]
  U2 = Mini-360 DC-DC Buck converter [package=THT]
  U3 = ESP32-38PinWide [part_number=ESP32-38PinWide]
  M1 = DC Motor  # not connected
  U5 = JST XH 4A 2.54mm [package=THT]
  Part3 = Current Sensor 5A
  J4 = Terminal Block - 2 pins [package=THT]
  DRV8871 = Adafruit DRV8871 [part_number="Adafruit #3190"]

nets (from the pcb view):
  N1: JP1.3, U3.GPIO17
  N2: JP1.5, U3.GPIO16
  N3: JP1.6, U3.GPIO5
  N4: JP1.7, U3.GPIO4
  GND: JP1.8, U2.IN-, U2.OUT-, U3.GND, U5.pin4, Part3.1, Part3.GND, J4.Line_2, DRV8871.GND, DRV8871.VMOTOR, DRV8871.OUT2, DRV8871.OUT1
  N5: JP1.9, U3.GPIO0
  N6: JP1.10, U3.GPIO2
  N7: U2.IN+, U3.GPIO13, Part3.2, Part3.OUT, J4.Line_1
  VIN: U2.OUT+, U3.VIN, Part3.VCC
  N8: U3.3.3, U5.pin3
  N9: U3.GPIO32, DRV8871.IN1
  N10: U3.GPIO33, DRV8871.IN2
  N11: U3.GPIO21, U5.pin1
  N12: U3.GPIO22, U5.pin2

notes:
  Keypad : AutoHelm 800
  HBridge : DRV8871
  Current Sensor : ACS712
  Power Down : Mini-360
  déplacer g25 en G13 pour gagner sur gnd ?

custom parts:
  Mini-360 DC-DC Buck converter: Mini-360 DC-DC Buck converter. Tiny buck step down voltage converter, input voltage 4.75 to 23V output 1 to 17V adjustable. Available from ebay and the like.
  ESP32-38PinWide: Generic 38-Pin ESP32 with wide format (only access to one side of pins on a breadboard) based on Stephen Lilley's HiLetgo ESP-WROOM-32 ESP32 ESP-32S Development Board.
  JST XH 4A 2.54mm: 4 Pin JST XH connector
  Terminal Block - 2 pins: Generic Screw Terminal 5mm
  Adafruit DRV8871: Crank up your robotics with powerful Adafruit DRV8871 motor driver breakout board. This motor driver has a lot of great specs that make it useful for a wide variety of mechatronics. In particular, the simple resistor-set current limiting and auto-magic PWM support make it super easy to use. Check out the specs for the DRV8871: 6.5V to 45V motor power voltage Up to 5.5V logic level on IN pins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
