# Fritzing sketch Autohelm 800 ESP32 Retrofit v4 (saved by Fritzing 0.9.6b)
circuit board: 6.84889cm x 5.57906cm

parts:
  Keyboard = Header 5x2 [package=avr_icsp]
  Step_Down = Mini-360 DC-DC Buck converter [package=THT]
  AUTOPILOT = ESP32-38PinWide [part_number=ESP32-38PinWide]
  9_Axes = JST XH 4A 2.54mm [package=THT]
  12_V = Terminal Block - 2 pins [package=THT]
  DRV8871 = Adafruit DRV8871 [part_number="Adafruit #3190"]
  END_2 = JST XH 2A male [form="♂ (male)" package=THT]
  END_1 = JST XH 2A male [form="♂ (male)" package=THT]
  Diode = Diode [package=diode-1n4148]

nets:
  N1: Keyboard.3, AUTOPILOT.GPIO17
  N2: Keyboard.5, AUTOPILOT.GPIO16
  N3: Keyboard.6, AUTOPILOT.GPIO5
  N4: Keyboard.7, AUTOPILOT.GPIO4
  GND: Keyboard.8, Step_Down.IN-, AUTOPILOT.GND, 9_Axes.pin4, 12_V.Line_2, DRV8871.GND, END_2.pin2, END_1.pin2
  N5: Keyboard.9, AUTOPILOT.GPIO0
  N6: Keyboard.10, AUTOPILOT.GPIO2
  N7: Step_Down.IN+, 12_V.Line_1, DRV8871.VMOTOR
  N8: Step_Down.OUT+, Diode.A
  N9: AUTOPILOT.3.3, 9_Axes.pin3
  N10: AUTOPILOT.GPIO32, DRV8871.IN1
  N11: AUTOPILOT.GPIO33, DRV8871.IN2
  N12: AUTOPILOT.GPIO14, END_1.pin1
  N13: AUTOPILOT.GPIO9, END_2.pin1
  N14: AUTOPILOT.VIN, Diode.C
  N15: AUTOPILOT.GPIO21, 9_Axes.pin1
  N16: AUTOPILOT.GPIO22, 9_Axes.pin2

notes:
  Keypad : AutoHelm 800
  HBridge : DRV8871
  End stops
  Power Down : Mini-360

custom parts:
  Mini-360 DC-DC Buck converter: Mini-360 DC-DC Buck converter. Tiny buck step down voltage converter, input voltage 4.75 to 23V output 1 to 17V adjustable. Available from ebay and the like.
  ESP32-38PinWide: Generic 38-Pin ESP32 with wide format (only access to one side of pins on a breadboard) based on Stephen Lilley's HiLetgo ESP-WROOM-32 ESP32 ESP-32S Development Board.
  JST XH 4A 2.54mm: 4 Pin JST XH connector
  Terminal Block - 2 pins: Generic Screw Terminal 5mm
  Adafruit DRV8871: Crank up your robotics with powerful Adafruit DRV8871 motor driver breakout board. This motor driver has a lot of great specs that make it useful for a wide variety of mechatronics. In particular, the simple resistor-set current limiting and auto-magic PWM support make it super easy to use. Check out the specs for the DRV8871: 6.5V to 45V motor power voltage Up to 5.5V logic level on IN pins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
  JST XH 2A male: JST XH-2A
