# Fritzing sketch Autohelm 800 ESP32 Retrofit (saved by Fritzing 0.9.6b)
circuit board: 8.46667cm x 5.64444cm

parts:
  L298N1 = L298N DC motor driver
  JP1 = Header 5x2 [package=avr_icsp]
  LOLIN32_LITE = Wemos Lolin32lite
  QMC5883L = Boladge HMC5883L Compass Module
  R1 = Resistor [tolerance=±5% power=0.25 resistance=222k package=THT]
  R2 = Resistor [tolerance=±5% power=0.25 resistance=10k package=THT]
  R5 = Resistor [tolerance=±5% power=0.25 resistance=100k package=THT]
  R4 = Resistor [tolerance=±5% power=0.25 resistance=100k package=THT]
  R3 = Resistor [tolerance=±5% power=0.25 resistance=100k package=THT]
  J1 = Power Jack [package=power_jack_smd]
  M1 = DC Motor
  U2 = Mini-360 DC-DC Buck converter [package=THT]
  Part1 = Adafruit ICM20948  # not connected

nets:
  N1: L298N1.OUT3, M1.pin_2
  N2: L298N1.OUT4, M1.pin_1
  N3: L298N1.12V, J1.GNDBREAK
  GND: L298N1.GND, QMC5883L.GND, J1.GND, U2.IN-
  N4: L298N1.5V, U2.IN+
  N5: L298N1.ENA, LOLIN32_LITE.pin_22
  N6: L298N1.IN1, LOLIN32_LITE.pin_21
  N7: L298N1.IN2, LOLIN32_LITE.pin_20
  N8: JP1.3, LOLIN32_LITE.pin_13, R5.Pin_0, R4.Pin_0, R3.Pin_0
  N9: JP1.5, LOLIN32_LITE.pin_10, R5.Pin_1
  N10: JP1.6, R1.Pin_1
  N11: JP1.7, LOLIN32_LITE.pin_11, R4.Pin_1
  N12: JP1.8, LOLIN32_LITE.pin_16
  N13: JP1.9, LOLIN32_LITE.pin_12, R3.Pin_1
  N14: JP1.10, R2.Pin_1
  N15: LOLIN32_LITE.pin_14, U2.OUT+
  N16: LOLIN32_LITE.pin_15, U2.OUT-
  N17: LOLIN32_LITE.pin_26, QMC5883L.SDA
  N18: LOLIN32_LITE.pin_27, QMC5883L.SCL
  N19: LOLIN32_LITE.pin_28, QMC5883L.VCC, R1.Pin_0, R2.Pin_0

custom parts:
  L298N DC motor driver: 2x DC motor driver with 78M05 positive voltage regulator (7..35 V) L298N: max 46 V, 2 A Set 5 V Enable jumper to enable 5 V regultor (needed for the L298N) and +5 V output at screw terminal or supply external +5 V at screw terminal Set ENA and/or ENB to +5 V to enable motor permanently or supply ENA and/or ENB with PWM signal IN1 and IN2 set rotation directory for motor A (OUT1/OUT2) IN2 and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
  Wemos Lolin32lite: Wemos Lolinlite32 wifi and blue tooth board based on the ESP-32 cpu, digital I/Os 19, analog inputs 6, clock 240mhz, Flash 4Mbytes, lipo battery charger (500ma connection broken out on breadboard but not pcb), usb.
  Boladge HMC5883L Compass Module: Cheap digital compass module
  Mini-360 DC-DC Buck converter: Mini-360 DC-DC Buck converter. Tiny buck step down voltage converter, input voltage 4.75 to 23V output 1 to 17V adjustable. Available from ebay and the like.
