# Fritzing sketch Autohelm 800 Keyboard (saved by Fritzing 0.9.6b)

parts:
  +1 = Round Pushbutton
  -1 = Round Pushbutton
  -10 = Round Pushbutton
  +10 = Round Pushbutton
  AUTO = Round Pushbutton
  STANDBY = Round Pushbutton
  LED1 = LED - 5mm [color="Red (633nm)" current=0.030 package="5 mm [THT]"]
  JP1 = Header 5x2 [package=avr_icsp]

nets:
  N1: +1.leg0, -1.leg1, JP1.5
  N2: +1.leg1, +10.leg1, AUTO.leg1, JP1.6
  N3: -1.leg0, -10.leg0
  N4: -10.leg1, +10.leg0, JP1.7
  N5: AUTO.leg0, STANDBY.leg1, JP1.9
  N6: STANDBY.leg0, JP1.10
  N7: LED1.cathode, JP1.8
  N8: LED1.anode, JP1.3

notes:
  Autohelm 800 Keyboard
